// Logisim project Cache - Nicholas Treynor.circ as structural Verilog: 13 circuits, main circuit main
module main (
  input  EnableTestHalting,
  output [9:0] CorrectCounter,
  output [9:0] HitCounter,
  output [9:0] MissCounter,
  output [9:0] TestNumber,
  output [7:0] ByteRead,
  output [7:0] CorrectByteRead,
  output Halt
);

  wire and_3_out, and_4_out, and_5_out, CLK, CmdIsRead, Correct, CpuRead, CpuWrite, DidContain, HaltTesting,
       MaxItersReached, MemRead, MemWrite, not_1_out, not_2_out, not_4_out, NotDoneTesting, Ok2Count,
       or_1_out, Ready;
  wire [7:0] CpuWriteValue, MemAddress;
  wire [9:0] CpuAddress;
  wire [31:0] Line2Mem, LineFromMem;

  not not_1 (not_1_out, Ready);
  Clock_part clock_1 (.out(CLK));
  or or_1 (or_1_out, MaxItersReached, Ready);
  Counter #(.width(4), .max('h9)) MaxClocks (
    .load(Ready), .D(4'b0001), .count(not_1_out), .carry(MaxItersReached), .clk(CLK));  // open: Q, clr
  and and_1 (HaltTesting, EnableTestHalting, CmdIsRead, not_2_out);
  not not_2 (not_2_out, Correct);
  not not_3 (NotDoneTesting, Halt);
  Inputs inputs_1 (
    .HaltTesting(HaltTesting), .Ready(or_1_out), .CLK(CLK), .Done(Halt), .Read(CpuRead), .Write(CpuWrite),
    .Address(CpuAddress), .Value(CpuWriteValue), .TestNumber(TestNumber));
  Cache cache_1 (
    .CpuAddress(CpuAddress), .CpuRead(CpuRead), .CpuWrite(CpuWrite), .CpuWriteValue(CpuWriteValue),
    .CLK(CLK), .Ready(Ready), .DidContain(DidContain), .ByteRead(ByteRead), .MemAddress(MemAddress),
    .MemRead(MemRead), .MemWrite(MemWrite), .LineFromMem(LineFromMem), .Line2Mem(Line2Mem));
  // Probe on CpuRead
  // Probe on CpuWrite
  // Probe on CpuAddress
  // Probe on CpuWriteValue
  // Probe on TestNumber
  // Probe on CorrectByteRead
  // Probe on Correct
  // Probe on Ready
  // Probe on DidContain
  // Probe on ByteRead
  // Probe on MemAddress
  // Probe on MemRead
  // Probe on MemWrite
  // Probe on HitCounter
  // Probe on LineFromMem
  // Probe on Line2Mem
  not not_4 (not_4_out, HaltTesting);
  RAM #(.dataWidth(32), .bus("separate")) ram_1 (
    .addr(MemAddress), .din(Line2Mem), .data(LineFromMem), .str(MemWrite), .clk(CLK), .ld(MemRead));  // open: sel, clr
  and and_2 (Ok2Count, Ready, not_4_out, NotDoneTesting);
  and and_3 (and_3_out, Correct, Ok2Count);
  and and_4 (and_4_out, DidContain, Ok2Count);
  and and_5 (and_5_out, MemRead, NotDoneTesting);
  Checker checker_1 (
    .TestNumber(TestNumber), .YourByteRead(ByteRead), .CmdIsRead(CmdIsRead),
    .CorrectByteRead(CorrectByteRead), .Correct(Correct));
  Counter #(.width(10), .max('h3ff)) u_CorrectCounter (
    .count(and_3_out), .Q(CorrectCounter), .clk(CLK));  // open: load, D, carry, clr
  Counter #(.width(10), .max('h3ff)) u_HitCounter (
    .count(and_4_out), .Q(HitCounter), .clk(CLK));  // open: load, D, carry, clr
  Counter #(.width(10), .max('h3ff)) u_MissCounter (
    .count(and_5_out), .Q(MissCounter), .clk(CLK));  // open: load, D, carry, clr
  // Probe on CorrectCounter
  // Probe on HitCounter
  // Probe on MissCounter

  // Other names for the same wires on the sheet: DoneTesting = Halt

  // Notes on the sheet:
  //   Nicholas Treynor - 915432828
  //   Hannan Waliullah - 915234550
  //   Your Answer Inside Here
endmodule

module Checker (
  input  [9:0] TestNumber,
  input  [7:0] YourByteRead,
  output CmdIsRead,
  output [7:0] CorrectByteRead,
  output Correct
);

  wire comparator_1_eq;
  wire [9:0] subtractor_1_out;

  // Probe on TestNumber
  Subtractor #(.width(10)) subtractor_1 (.a(TestNumber), .b(10'h1), .out(subtractor_1_out));  // open: bin, bout
  ROM #(.addrWidth(10), .dataWidth(9)) rom_1 (
    .addr(subtractor_1_out), .data({CmdIsRead, CorrectByteRead}));  // open: sel
  Comparator #(.mode("unsigned")) comparator_1 (
    .a(YourByteRead), .b(CorrectByteRead), .eq(comparator_1_eq));  // open: gt, lt
  and and_1 (Correct, comparator_1_eq, CmdIsRead);

  // Other names for the same wires on the sheet: Test_Number[9:0] = TestNumber

  // Notes on the sheet:
  //   Read Solutions
  //   contents of rom_1 (hex, n*v repeats v):
  //   1a3 1dc 6b 125 1 75 1dc 1c3 d8 1ab 77 70 b 33 10b d8 1c3 c9 174 58 bf 153 199 f 9d 56 1bb 13b 89 16c
  //   180 66 b6 0 e 107 1bf 1d8 167 89 118 55 1a2 e8 f2 1c3 d7 142 6b 73 1ab 18c 70 f da 1c3 14c 1d8 d5 4
  //   1d8 16b b1 1f4 1f2 ff 1da 50 1da 6d c2 f8 155 1c6 1f8 82 ae 1ff 35 d0 16b 1ae 72 175 3a 37 1ff 173
  //   1d0 158 167 1d5 96 a1 1f4 1c3 e6 cc 155 80 170 5d 1e6 166 e5 1ae 15 a2 ab 170 10f 13b 24 150 fc 33
  //   58 133 36 69 170 69 1c3 14c e4 80 e8 1ab 15d 158 1fc 135 cd 1e5 5a e0 104 73 8c 14c 68 99 ed 1a6
endmodule

module Inputs (
  input  HaltTesting,
  input  Ready,
  input  CLK,
  output Done,
  output Read,
  output Write,
  output [9:0] Address,
  output [7:0] Value,
  output [9:0] TestNumber
);

  wire and_1_out, not_1_out, not_2_out;

  not not_1 (not_1_out, HaltTesting);
  not not_2 (not_2_out, Done);
  Counter #(.width(10), .max('h3ff), .ongoal("stay")) u_TestNumber (
    .count(and_1_out), .Q(TestNumber), .clk(CLK));  // open: load, D, carry, clr
  and and_1 (and_1_out, not_1_out, Ready, not_2_out);
  ROM #(.addrWidth(10), .dataWidth(21)) rom_1 (
    .addr(TestNumber), .data({Done, Read, Write, Address, Value}));  // open: sel

  // Notes on the sheet:
  //   contents of rom_1 (hex, n*v repeats v):
  //   80882 83fe6 4306b 83e0e 43701 42275 8280f 80304 41bd8 84371 43f77 41d70 4250b 44733 8253d 440d8
  //   82691 440c9 83d7c 43558 446bf 83837 842c9 43e0f 4059d 41556 80166 833b0 43a89 83142 8361c 42e66
  //   43eb6 42c00 43a0e 8165c 84682 8092a 83907 41f89 817b0 40855 82056 425e8 43ff2 8039f 42bd7 82137
  //   4416b 40273 8324a 814e4 44570 41c0f 429da 82640 8069c 8099e 414d5 41004 81beb 84113 419b1 81add
  //   83f35 425ff 829cd 40250 82945 4366d 40cc2 444f8 80814 81156 8446d 42a82 42bae 82578 41135 405d0
  //   8304b 82b3a 40972 822ba 4443a 42337 82506 80bd3 80560 83552 83955 81434 43096 43da1 81aa2 80305
  //   428e6 428cc 808a2 40e80 845f0 4215d 82765 82e29 40be5 82b74 42715 417a2 41fab 8452f 81c0a 83325
  //   44624 80205 42dfc 41333 40958 81348 42736 41069 84510 44669 826dd 8067e 408e4 44680 444e8 832ad
  //   821f8 83509 82d46 81184 432cd 80b77 4005a 440e0 81ea0 43d73 42b8c 80624 41468 42699 415ed 80fc1 0
  //   100000
endmodule

module Cache (
  input  [9:0] CpuAddress,
  input  CpuRead,
  input  CpuWrite,
  input  [7:0] CpuWriteValue,
  input  CLK,
  input  [31:0] LineFromMem,
  output Ready,
  output DidContain,
  output [7:0] ByteRead,
  output [7:0] MemAddress,
  output MemRead,
  output MemWrite,
  output [31:0] Line2Mem
);

  wire CpuRead_t, CpuWrite_t, DidContainInput, Evicting_Dirty, Evicting_Dirty_0, Evicting_Dirty_1,
       New_State1, New_State2, New_State3, New_State4, New_State5, New_State6, not_1_out, not_2_out, State2,
       State3, State4, State5, State6, TagMatch0, TagMatch1;
  wire [6:0] Evicting_Tag, Oldest_Tag_0, Oldest_Tag_1;
  wire [7:0] ByteRead_0, ByteRead_1, CpuWriteValue_t;
  wire [9:0] CpuAddress_t;
  wire [31:0] Data1, Data2, StoredLineFromMem;

  Register StoreCPUWriteValue (.D(CpuWriteValue), .en(Ready), .Q(CpuWriteValue_t), .clk(CLK));  // open: clr
  Register #(.width(32)) StoreCPUAdress (.D(LineFromMem), .en(State3), .Q(StoredLineFromMem), .clk(CLK));  // open: clr
  Register #(.width(10)) StoreCPUAdress_2 (.D(CpuAddress), .en(Ready), .Q(CpuAddress_t), .clk(CLK));  // open: clr
  Register #(.width(1)) register_1 (.D(CpuRead), .en(Ready), .Q(CpuRead_t), .clk(CLK));  // open: clr
  Register #(.width(1)) register_2 (.D(CpuWrite), .en(Ready), .Q(CpuWrite_t), .clk(CLK));  // open: clr
  not not_1 (not_1_out, CpuAddress_t[2]);
  Register #(.width(1)) State1 (.D(New_State1), .Q(Ready), .clk(CLK));  // open: en, clr
  Register #(.width(1)) u_State2 (.D(New_State2), .Q(State2), .clk(CLK));  // open: en, clr
  Register #(.width(1)) u_State3 (.D(New_State3), .Q(State3), .clk(CLK));  // open: en, clr
  Register #(.width(1)) u_State4 (.D(New_State4), .Q(State4), .clk(CLK));  // open: en, clr
  Register #(.width(1)) u_State5 (.D(New_State5), .Q(State5), .clk(CLK));  // open: en, clr
  Register #(.width(1)) u_State6 (.D(New_State6), .Q(State6), .clk(CLK));  // open: en, clr
  Set_0 set_0_1 (
    .Tag(CpuAddress_t[9:3]), .Set(CpuAddress_t[2]), .Offset(CpuAddress_t[1:0]), .CpuRead(CpuRead_t),
    .CpuWrite(CpuWrite_t), .CLK(CLK), .LineFromMemInput(StoredLineFromMem), .CpuWriteValue(CpuWriteValue_t),
    .TagMatchFound(TagMatch0), .Evicting_Dirty(Evicting_Dirty_0), .Oldest_Tag_Present(Oldest_Tag_0),
    .Oldest_Data_Present(Data1), .ByteRead(ByteRead_0));  // open: Evicting, Oldest
  Set_0 set_0_2 (
    .Tag(CpuAddress_t[9:3]), .Set(not_1_out), .Offset(CpuAddress_t[1:0]), .CpuRead(CpuRead_t),
    .CpuWrite(CpuWrite_t), .CLK(CLK), .LineFromMemInput(StoredLineFromMem), .CpuWriteValue(CpuWriteValue_t),
    .TagMatchFound(TagMatch1), .Evicting_Dirty(Evicting_Dirty_1), .Oldest_Tag_Present(Oldest_Tag_1),
    .Oldest_Data_Present(Data2), .ByteRead(ByteRead_1));  // open: Evicting, Oldest
  Clock clock_1 (
    .State1(Ready), .State2(State2), .State3(State3), .State4(State4), .State5(State5), .State6(State6),
    .State1o(New_State1), .State2o(New_State2), .State3o(New_State3), .State4o(New_State4),
    .State5o(New_State5), .State6o(New_State6));
  Multiplexer #(.width(8), .enable("false")) multiplexer_1 (
    .in0(ByteRead_0), .in1(ByteRead_1), .out(ByteRead), .sel(CpuAddress_t[2]));
  Multiplexer #(.width(7), .enable("false")) multiplexer_2 (
    .in0(Oldest_Tag_0), .in1(Oldest_Tag_1), .out(Evicting_Tag), .sel(CpuAddress_t[2]));
  Register #(.width(1)) StoreDidContain (.D(DidContainInput), .en(State2), .Q(DidContain), .clk(CLK));  // open: clr
  or or_1 (Evicting_Dirty, Evicting_Dirty_0, Evicting_Dirty_1);
  or or_2 (DidContainInput, TagMatch0, TagMatch1);
  not not_2 (not_2_out, DidContain);
  Multiplexer #(.width(8), .enable("false")) multiplexer_3 (
    .in0(CpuAddress_t[9:2]), .in1({Evicting_Tag, CpuAddress_t[2]}), .out(MemAddress), .sel(State2));
  and and_1 (MemRead, not_2_out, State3);
  and and_2 (MemWrite, Evicting_Dirty, State2);
  // AND_Gate and_3 has open pins: in0=Evicting_Dirty, in1=State3, out=open
  Multiplexer #(.width(32), .enable("false")) multiplexer_4 (
    .in0(Data1), .in1(Data2), .out(Line2Mem), .sel(CpuAddress_t[2]));

  // Other names for the same wires on the sheet: Tag[6:0] = CpuAddress_t[9:3]; Set = CpuAddress_t[2];
  //   Offset[1:0] = CpuAddress_t[1:0]; CpuAddressInput[9:0] = CpuAddress; CpuReadInput = CpuRead;
  //   CpuWriteInput = CpuWrite; CpuWriteValueInput[7:0] = CpuWriteValue; Mem_Adress[7:0] = MemAddress; State1 = Ready

  // Notes on the sheet:
  //   Address Bits = 10
  //   Line Size = 4
  //   W = 3
  //   Num Sets = 2
  //   C =4*3*2 = 24bytes
  //   Nicholas Treynor - 915432828
  //   Hannan Waliullah - 915234550
  //   Tag bits = 7
  //   Set 01 (2 of 2)
  //   Set 00 (1 of 2)
  //   Must add clock cycles to these:
endmodule

module Set_0 (
  input  [6:0] Tag,
  input  Set,
  input  [1:0] Offset,
  input  CpuRead,
  input  CpuWrite,
  input  CLK,
  input  [31:0] LineFromMemInput,
  input  [7:0] CpuWriteValue,
  output TagMatchFound,
  output Evicting,
  output Evicting_Dirty,
  output [6:0] Oldest_Tag_Present,
  output [31:0] Oldest_Data_Present,
  output [1:0] Oldest,
  output [7:0] ByteRead
);

  wire and_1_out, and_2_out, and_3_out, and_4_out, and_5_out, and_6_out, and_9_out, and_10_out, and_11_out,
       comparator_1_eq, comparator_2_eq, comparator_3_eq, comparator_4_eq, comparator_5_eq, comparator_6_eq,
       comparator_13_eq, comparator_14_eq, comparator_15_eq, comparator_16_eq, comparator_17_eq,
       comparator_18_eq, Dirty_000__0, Dirty_001__1, Dirty_010__2, New_State1, New_State2, New_State3,
       New_State4, New_State5, New_State6, not_2_out, Oldest_Dirty_Bit, ON, or_1_out, or_2_out, Set_is_full,
       State1, State2, State3, State4, State5, State6, Valid_000__0, Valid_001__1, Valid_010__2,
       Youngest_Tag_Access;
  wire [1:0] Age_000__0, Age_001__1, Age_010__2, Youngest;
  wire [2:0] comparator_7_eq, comparator_10_eq;
  wire [6:0] Tag_000__0, Tag_001__1, Tag__010___2;
  wire [7:0] ByteRead0, ByteRead1, ByteRead2;
  wire [31:0] Data_Output_0, Data_Output_1, Data_Output_2;

  not not_1 (ON, Set);
  Comparator #(.width(2), .mode("unsigned")) comparator_1 (
    .a(Age_000__0), .b(2'b10), .eq(comparator_1_eq));  // open: gt, lt
  Comparator #(.width(2), .mode("unsigned")) comparator_2 (
    .a(Age_001__1), .b(2'b10), .eq(comparator_2_eq));  // open: gt, lt
  Comparator #(.width(2), .mode("unsigned")) comparator_3 (
    .a(Age_010__2), .b(2'b10), .eq(comparator_3_eq));  // open: gt, lt
  and and_1 (and_1_out, Dirty_000__0, comparator_1_eq);
  and and_2 (and_2_out, Dirty_001__1, comparator_2_eq);
  and and_3 (and_3_out, Dirty_010__2, comparator_3_eq);
  Register #(.width(1)) u_State1 (.D(New_State1), .Q(State1), .clk(CLK));  // open: en, clr
  Register #(.width(1)) u_State2 (.D(New_State2), .Q(State2), .clk(CLK));  // open: en, clr
  Register #(.width(1)) u_State3 (.D(New_State3), .Q(State3), .clk(CLK));  // open: en, clr
  Register #(.width(1)) u_State4 (.D(New_State4), .Q(State4), .clk(CLK));  // open: en, clr
  Register #(.width(1)) u_State5 (.D(New_State5), .Q(State5), .clk(CLK));  // open: en, clr
  Register #(.width(1)) u_State6 (.D(New_State6), .Q(State6), .clk(CLK));  // open: en, clr
  Block_000__0 block_000_0_1 (
    .CpuRead(CpuRead), .CpuWrite(CpuWrite), .Crct_Tag_Present(TagMatchFound), .The_set_is_full(Set_is_full),
    .Input_Tag(Tag), .CLK(CLK), .Starting_Age(2'b00), .Youngest_Age_Input(Youngest_Tag_Access),
    .Offset(Offset), .MemInput(LineFromMemInput), .CPUWriteValue(CpuWriteValue), .State_4(State4),
    .State_5(State5), .State_6(State6), .Set(ON), .Tag_Output(Tag__010___2), .Valid_Output(Valid_010__2),
    .Dirty_Output(Dirty_010__2), .Age_Output(Age_010__2), .Data_Output(Data_Output_2), .Byte_Output(ByteRead2));
  or or_1 (or_1_out, and_1_out, and_2_out, and_3_out);
  Block_000__0 block_000_0_2 (
    .CpuRead(CpuRead), .CpuWrite(CpuWrite), .Crct_Tag_Present(TagMatchFound), .The_set_is_full(Set_is_full),
    .Input_Tag(Tag), .CLK(CLK), .Starting_Age(2'b10), .Youngest_Age_Input(Youngest_Tag_Access),
    .Offset(Offset), .MemInput(LineFromMemInput), .CPUWriteValue(CpuWriteValue), .State_4(State4),
    .State_5(State5), .State_6(State6), .Set(ON), .Tag_Output(Tag_000__0), .Valid_Output(Valid_000__0),
    .Dirty_Output(Dirty_000__0), .Age_Output(Age_000__0), .Data_Output(Data_Output_0), .Byte_Output(ByteRead0));
  Block_000__0 block_000_0_3 (
    .CpuRead(CpuRead), .CpuWrite(CpuWrite), .Crct_Tag_Present(TagMatchFound), .The_set_is_full(Set_is_full),
    .Input_Tag(Tag), .CLK(CLK), .Starting_Age(2'b01), .Youngest_Age_Input(Youngest_Tag_Access),
    .Offset(Offset), .MemInput(LineFromMemInput), .CPUWriteValue(CpuWriteValue), .State_4(State4),
    .State_5(State5), .State_6(State6), .Set(ON), .Tag_Output(Tag_001__1), .Valid_Output(Valid_001__1),
    .Dirty_Output(Dirty_001__1), .Age_Output(Age_001__1), .Data_Output(Data_Output_1), .Byte_Output(ByteRead1));
  Clock clock_1 (
    .State1(State1), .State2(State2), .State3(State3), .State4(State4), .State5(State5), .State6(State6),
    .State1o(New_State1), .State2o(New_State2), .State3o(New_State3), .State4o(New_State4),
    .State5o(New_State5), .State6o(New_State6));
  Comparator #(.width(7), .mode("unsigned")) comparator_4 (
    .a(Tag_000__0), .b(Tag), .eq(comparator_4_eq));  // open: gt, lt
  Comparator #(.width(7), .mode("unsigned")) comparator_5 (
    .a(Tag_001__1), .b(Tag), .eq(comparator_5_eq));  // open: gt, lt
  Comparator #(.width(7), .mode("unsigned")) comparator_6 (
    .a(Tag__010___2), .b(Tag), .eq(comparator_6_eq));  // open: gt, lt
  Comparator #(.width(2), .mode("unsigned")) comparator_7 (
    .a(Age_000__0), .b(2'b00), .eq(comparator_7_eq[0]));  // open: gt, lt
  Comparator #(.width(2), .mode("unsigned")) comparator_8 (
    .a(Age_001__1), .b(2'b00), .eq(comparator_7_eq[1]));  // open: gt, lt
  Comparator #(.width(2), .mode("unsigned")) comparator_9 (
    .a(Age_010__2), .b(2'b00), .eq(comparator_7_eq[2]));  // open: gt, lt
  Comparator #(.width(2), .mode("unsigned")) comparator_10 (
    .a(Age_000__0), .b(2'b10), .eq(comparator_10_eq[0]));  // open: gt, lt
  Comparator #(.width(2), .mode("unsigned")) comparator_11 (
    .a(Age_001__1), .b(2'b10), .eq(comparator_10_eq[1]));  // open: gt, lt
  Comparator #(.width(2), .mode("unsigned")) comparator_12 (
    .a(Age_010__2), .b(2'b10), .eq(comparator_10_eq[2]));  // open: gt, lt
  and and_4 (and_4_out, comparator_4_eq, Valid_000__0);
  and and_5 (and_5_out, comparator_5_eq, Valid_001__1);
  and and_6 (and_6_out, comparator_6_eq, Valid_010__2);
  BitFinder #(.width(3)) bitfinder_1 (.in(comparator_7_eq), .index(Youngest));  // open: found
  BitFinder #(.width(3)) bitfinder_2 (.in(comparator_10_eq), .index(Oldest));  // open: found
  or or_2 (or_2_out, and_4_out, and_5_out, and_6_out);
  and and_7 (TagMatchFound, ON, or_2_out);
  and and_8 (Set_is_full, Valid_000__0, Valid_001__1, Valid_010__2);
  Comparator #(.width(7), .mode("unsigned")) comparator_13 (
    .a(Tag), .b(Tag_000__0), .eq(comparator_13_eq));  // open: gt, lt
  Comparator #(.width(2), .mode("unsigned")) comparator_14 (
    .a(Age_000__0), .b(2'b00), .eq(comparator_14_eq));  // open: gt, lt
  Comparator #(.width(7), .mode("unsigned")) comparator_15 (
    .a(Tag), .b(Tag_001__1), .eq(comparator_15_eq));  // open: gt, lt
  Comparator #(.width(2), .mode("unsigned")) comparator_16 (
    .a(Age_001__1), .b(2'b00), .eq(comparator_16_eq));  // open: gt, lt
  Comparator #(.width(7), .mode("unsigned")) comparator_17 (
    .a(Tag), .b(Tag__010___2), .eq(comparator_17_eq));  // open: gt, lt
  Comparator #(.width(2), .mode("unsigned")) comparator_18 (
    .a(Age_010__2), .b(2'b00), .eq(comparator_18_eq));  // open: gt, lt
  and and_9 (and_9_out, comparator_13_eq, Valid_000__0, comparator_14_eq);
  and and_10 (and_10_out, comparator_15_eq, Valid_001__1, comparator_16_eq);
  and and_11 (and_11_out, comparator_17_eq, Valid_010__2, comparator_18_eq);
  Multiplexer #(.select(2), .width(8), .enable("false")) multiplexer_1 (
    .in0(ByteRead0), .in1(ByteRead1), .in2(ByteRead2), .out(ByteRead), .sel(Youngest));  // open: in3
  or or_3 (Youngest_Tag_Access, and_9_out, and_10_out, and_11_out);
  Multiplexer #(.select(2), .width(7), .enable("false")) multiplexer_2 (
    .in0(Tag_000__0), .in1(Tag_001__1), .in2(Tag__010___2), .out(Oldest_Tag_Present), .sel(Oldest));  // open: in3
  Multiplexer #(.select(2), .width(32), .enable("false")) multiplexer_3 (
    .in0(Data_Output_0), .in1(Data_Output_1), .in2(Data_Output_2), .out(Oldest_Data_Present), .sel(Oldest));  // open: in3
  Multiplexer #(.select(2), .enable("false")) multiplexer_4 (
    .in0(Dirty_000__0), .in1(Dirty_001__1), .in2(Dirty_010__2), .out(Oldest_Dirty_Bit), .sel(Oldest));  // open: in3
  not not_2 (not_2_out, TagMatchFound);
  and u_Evicting (Evicting, not_2_out, Set_is_full, ON);
  and and_12 (Evicting_Dirty, Evicting, Oldest_Dirty_Bit);

  // Other names for the same wires on the sheet: Correct_Tag_Present = TagMatchFound; Input_Tag[6:0] = Tag;
  //   Oldest_Data[31:0] = Oldest_Data_Present; Oldest_Tag[6:0] = Oldest_Tag_Present
endmodule

module Block_000__0 (
  input  CpuRead,
  input  CpuWrite,
  input  Crct_Tag_Present,
  input  The_set_is_full,
  input  [6:0] Input_Tag,
  input  CLK,
  input  [1:0] Starting_Age,
  input  Youngest_Age_Input,
  input  [1:0] Offset,
  input  [31:0] MemInput,
  input  [7:0] CPUWriteValue,
  input  State_4,
  input  State_5,
  input  State_6,
  input  Set,
  output [6:0] Tag_Output,
  output Valid_Output,
  output Dirty_Output,
  output [1:0] Age_Output,
  output [31:0] Data_Output,
  output [7:0] Byte_Output
);

  wire and_1_out, and_2_out, and_4_out, and_6_out, and_8_out, and_9_out, and_11_out, and_12_out, and_14_out,
       Block_Being_Replaced, Block_Being_Set, Block_Selected, ClockState, comparator_1_eq, comparator_2_eq,
       comparator_3_eq, comparator_4_eq, multiplexer_1_out, New_Dirty_Bit, New_Valid_Bit, not_1_out,
       not_2_out, Overwriting, Read_Now;
  wire [1:0] multiplexer_2_out, New_Age;
  wire [6:0] New_Tag;
  wire [7:0] New_Data_1, New_Data_2, New_Data_3, New_Data_4, Overwritten_New_Data_1, Overwritten_New_Data_2,
       Overwritten_New_Data_3, Overwritten_New_Data_4, Read_Write_New_Data1, Read_Write_New_Data2,
       Read_Write_New_Data3, Read_Write_New_Data4;

  Comparator #(.width(7), .mode("unsigned")) comparator_1 (
    .a(Tag_Output), .b(Input_Tag), .eq(comparator_1_eq));  // open: gt, lt
  Counter #(.width(1), .max('h1), .ongoal("stay")) HitCounter (
    .Q(ClockState), .clk(CLK));  // open: load, D, count, carry, clr
  and and_1 (and_1_out, Set, State_5);
  and and_2 (and_2_out, Set, State_6);
  Multiplexer #(.enable("false")) multiplexer_1 (
    .in0(1'b0), .in1(New_Valid_Bit), .out(multiplexer_1_out), .sel(ClockState));
  and and_3 (Read_Now, comparator_1_eq, CpuRead);
  and and_4 (and_4_out, Set, State_4);
  and and_5 (and_4_out, Set, State_4);
  and and_6 (and_6_out, Block_Selected, Valid_Output);
  Register #(.width(7)) Tag (.D(New_Tag), .Q(Tag_Output), .clk(CLK));  // open: en, clr
  Register #(.width(1)) Valid_Bit (.D(multiplexer_1_out), .Q(Valid_Output), .clk(CLK));  // open: en, clr
  Register #(.width(1)) Dirty_Bit (.D(New_Dirty_Bit), .Q(Dirty_Output), .clk(CLK));  // open: en, clr
  Multiplexer #(.width(2), .enable("false")) multiplexer_2 (
    .in0(Starting_Age), .in1(New_Age), .out(multiplexer_2_out), .sel(ClockState));
  Register #(.width(2)) Age (.D(multiplexer_2_out), .Q(Age_Output), .clk(CLK));  // open: en, clr
  New_Data_Bits new_data_bits_1 (
    .State_4(and_4_out), .BBr(Block_Being_Replaced), .BS(Block_Selected),
    .Current_Data_1(Data_Output[31:24]), .Current_Data_2(Data_Output[23:16]),
    .Curremt_Data_3(Data_Output[15:8]), .Current_Data_4(Data_Output[7:0]), .Offset(Offset),
    .MemInput(MemInput), .Output_Data_1(Overwritten_New_Data_1), .Output_Data_2(Overwritten_New_Data_2),
    .Output_Data_3(Overwritten_New_Data_3), .Output_Data_4(Overwritten_New_Data_4), .Overwriting(Overwriting));
  Read_Write read_write_1 (
    .CpuRead(CpuRead), .CpuWrite(CpuWrite), .BS(and_6_out), .State_5(and_1_out),
    .CpuWriteValue(CPUWriteValue), .Current_Data_1(Data_Output[31:24]), .Current_Data_2(Data_Output[23:16]),
    .Current_Data_3(Data_Output[15:8]), .Current_Data_4(Data_Output[7:0]), .Offset(Offset),
    .State_6(and_2_out), .Output_Data_1(Read_Write_New_Data1), .Output_Data_2(Read_Write_New_Data2),
    .Output_Data_3(Read_Write_New_Data3), .Output_Data_4(Read_Write_New_Data4), .Byte_Read(Byte_Output));
  Comparator #(.width(2), .mode("unsigned")) comparator_2 (
    .a(Age_Output), .b(2'b10), .eq(comparator_2_eq));  // open: gt, lt
  not not_1 (not_1_out, Crct_Tag_Present);
  Register Data_1 (.D(New_Data_1), .Q(Data_Output[31:24]), .clk(CLK));  // open: en, clr
  Register Data_2 (.D(New_Data_2), .Q(Data_Output[23:16]), .clk(CLK));  // open: en, clr
  Register Data_3 (.D(New_Data_3), .Q(Data_Output[15:8]), .clk(CLK));  // open: en, clr
  Register Data_4 (.D(New_Data_4), .Q(Data_Output[7:0]), .clk(CLK));  // open: en, clr
  and and_7 (Block_Being_Replaced, not_1_out, comparator_2_eq);
  and and_8 (and_8_out, Set, State_4);
  Multiplexer #(.width(8), .enable("false")) multiplexer_3 (
    .in0(Read_Write_New_Data1), .in1(Overwritten_New_Data_1), .out(New_Data_1), .sel(Overwriting));
  Multiplexer #(.width(8), .enable("false")) multiplexer_4 (
    .in0(Read_Write_New_Data2), .in1(Overwritten_New_Data_2), .out(New_Data_2), .sel(Overwriting));
  Multiplexer #(.width(8), .enable("false")) multiplexer_5 (
    .in0(Read_Write_New_Data3), .in1(Overwritten_New_Data_3), .out(New_Data_3), .sel(Overwriting));
  Multiplexer #(.width(8), .enable("false")) multiplexer_6 (
    .in0(Read_Write_New_Data4), .in1(Overwritten_New_Data_4), .out(New_Data_4), .sel(Overwriting));
  New_Age_Subcircuit new_age_subcircuit_1 (
    .Updating_Cycle(and_8_out), .Block_Selected(Block_Selected),
    .Block_Replacement_Occuring(Block_Being_Replaced), .Block_Age(Age_Output),
    .Block_Being_Set(Block_Being_Set), .Youngest_Age_Input(Youngest_Age_Input), .Updated_Block_Age(New_Age));
  Comparator #(.width(7), .mode("unsigned")) comparator_3 (
    .a(Tag_Output), .b(Input_Tag), .eq(comparator_3_eq));  // open: gt, lt
  and and_9 (and_9_out, Set, State_4);
  Comparator #(.width(2), .mode("unsigned")) comparator_4 (
    .a(Age_Output), .b(2'b10), .eq(comparator_4_eq));  // open: gt, lt
  and and_10 (Block_Selected, Crct_Tag_Present, comparator_3_eq);
  not not_2 (not_2_out, Valid_Output);
  and and_11 (and_11_out, Valid_Output, Block_Selected);
  and and_12 (and_12_out, Set, State_4);
  New_Valid_Subcircuit new_valid_subcircuit_1 (
    .Updating_Cycle(and_12_out), .Current_Valid_Bit(Valid_Output), .Block_Being_Set(Block_Being_Set),
    .Updated_Valid_Bit(New_Valid_Bit));
  New_Tag_Subcircuit new_tag_subcircuit_1 (
    .Updating_Cycle(and_9_out), .Block_Selected(Block_Selected),
    .Block_Replacement_Occuring(Block_Being_Replaced), .Block_Tag(Tag_Output), .New_Block_Tag(Input_Tag),
    .Block_Being_Set(Block_Being_Set), .Updated_Tag(New_Tag));
  and and_13 (Block_Being_Set, not_2_out, ~Crct_Tag_Present, Set, comparator_4_eq);  // AND_Gate
  and and_14 (and_14_out, Set, State_4);
  New_Dirty_Bit new_dirty_bit_1 (
    .Updating_Cycle(and_14_out), .Block_Selected(and_11_out),
    .Block_Replacement_Occuring(Block_Being_Replaced), .Current_Dirty_Bit(Dirty_Output),
    .Block_Being_Set(Block_Being_Set), .CpuRead(CpuRead), .CpuWrite(CpuWrite),
    .Updated_Dirty_Bit(New_Dirty_Bit));

  // Other names for the same wires on the sheet: ByteRead[7:0] = Byte_Output; Correct_Tag_Present = Crct_Tag_Present;
  //   Current_Age[1:0] = Age_Output; Current_Dirty_Bit = Dirty_Output; Current_Tag[6:0] = Tag_Output;
  //   Current_Valid_Bit = Valid_Output; Current_Data_4[7:0] = Data_Output[7:0];
  //   Current_Data_3[7:0] = Data_Output[15:8]; Current_Data_2[7:0] = Data_Output[23:16];
  //   Current_Data_1[7:0] = Data_Output[31:24]; LineFromMemInput[31:0] = MemInput; Set_is_full = The_set_is_full

  // Notes on the sheet:
  //   Could this be Asyncronious if we use this value on the clock cycle we change age?
  //   Don't think so, age updates on the new clock cycle.
endmodule

module New_Age_Subcircuit (
  input  Updating_Cycle,
  input  Block_Selected,
  input  Block_Replacement_Occuring,
  input  [1:0] Block_Age,
  input  Block_Being_Set,
  input  Youngest_Age_Input,
  output [1:0] Updated_Block_Age
);

  wire and_1_out, not_1_out, or_1_out;
  wire [1:0] adder_1_out, multiplexer_1_out, Output_age;

  Adder #(.width(2)) adder_1 (.a(Block_Age), .b(2'b01), .out(adder_1_out));  // open: cin, cout
  Multiplexer #(.width(2), .enable("false")) multiplexer_1 (
    .in0(adder_1_out), .in1(2'b00), .out(multiplexer_1_out), .sel(or_1_out));
  or or_1 (or_1_out, Block_Selected, Block_Being_Set, Block_Replacement_Occuring);
  and and_1 (and_1_out, Updating_Cycle, not_1_out);
  Multiplexer #(.width(2), .enable("false")) multiplexer_2 (
    .in0(Block_Age), .in1(multiplexer_1_out), .out(Output_age), .sel(and_1_out));
  not not_1 (not_1_out, Youngest_Age_Input);
  Multiplexer #(.select(2), .width(2), .enable("false")) multiplexer_3 (
    .in0(2'b00), .in1(2'b01), .in2(2'b10), .in3(2'b10), .out(Updated_Block_Age), .sel(Output_age));

  // Other names for the same wires on the sheet: Block_Being_Replaced = Block_Replacement_Occuring;
  //   Current_Age[1:0] = Block_Age; Updating = Updating_Cycle
endmodule

module New_Tag_Subcircuit (
  input  Updating_Cycle,
  input  Block_Selected,
  input  Block_Replacement_Occuring,
  input  [6:0] Block_Tag,
  input  [6:0] New_Block_Tag,
  input  Block_Being_Set,
  output [6:0] Updated_Tag
);

  wire or_1_out;
  wire [6:0] multiplexer_1_out;

  Multiplexer #(.width(7), .enable("false")) multiplexer_1 (
    .in0(Block_Tag), .in1(New_Block_Tag), .out(multiplexer_1_out), .sel(or_1_out));
  or or_1 (or_1_out, Block_Selected, Block_Being_Set, Block_Replacement_Occuring);
  Multiplexer #(.width(7), .enable("false")) multiplexer_2 (
    .in0(Block_Tag), .in1(multiplexer_1_out), .out(Updated_Tag), .sel(Updating_Cycle));

  // Other names for the same wires on the sheet: Block_Being_Replaced = Block_Replacement_Occuring;
  //   Current_Tag[6:0] = Block_Tag; New_Tag[6:0] = New_Block_Tag; Updating = Updating_Cycle
endmodule

module New_Valid_Subcircuit (
  input  Updating_Cycle,
  input  Current_Valid_Bit,
  input  Block_Being_Set,
  output Updated_Valid_Bit
);

  wire or_1_out;

  or or_1 (or_1_out, Current_Valid_Bit, Block_Being_Set);
  Multiplexer #(.enable("false")) multiplexer_1 (
    .in0(Current_Valid_Bit), .in1(or_1_out), .out(Updated_Valid_Bit), .sel(Updating_Cycle));

  // Other names for the same wires on the sheet: Updating = Updating_Cycle
endmodule

module New_Dirty_Bit (
  input  Updating_Cycle,
  input  Block_Selected,
  input  Block_Replacement_Occuring,
  input  Current_Dirty_Bit,
  input  Block_Being_Set,
  input  CpuRead,
  input  CpuWrite,
  output Updated_Dirty_Bit
);

  wire and_1_out, and_2_out, and_3_out, and_4_out, and_5_out, multiplexer_1_out, nand_1_out, or_1_out,
       or_2_out, or_3_out, or_4_out;

  or or_1 (or_1_out, Block_Replacement_Occuring, Block_Being_Set);
  and and_1 (and_1_out, or_1_out, CpuRead);
  or or_2 (or_2_out, Block_Replacement_Occuring, Block_Selected, Block_Being_Set);
  and and_2 (and_2_out, or_2_out, CpuWrite);
  and and_3 (and_3_out, Block_Selected, Block_Replacement_Occuring);
  nand nand_1 (nand_1_out, Block_Selected, CpuRead);
  and and_4 (and_4_out, or_4_out, Updating_Cycle);
  Multiplexer #(.enable("false")) multiplexer_1 (
    .in0(Current_Dirty_Bit), .in1(and_2_out), .out(multiplexer_1_out), .sel(and_5_out));
  and and_5 (and_5_out, nand_1_out, or_3_out, Updating_Cycle);
  or or_3 (or_3_out, Block_Replacement_Occuring, Block_Selected, Block_Being_Set);
  Multiplexer #(.enable("false")) multiplexer_2 (
    .in0(Current_Dirty_Bit), .in1(CpuWrite), .out(Updated_Dirty_Bit), .sel(and_4_out));
  or or_4 (or_4_out, and_3_out, Block_Being_Set);

  // Other names for the same wires on the sheet: Block_Being_Replaced = Block_Replacement_Occuring;
  //   Updating = Updating_Cycle

  // Notes on the sheet:
  //   Should become a 0
  //   Should become a 1
  //   Don't update at all
  //   Note: Double Check This Logic Later
endmodule

module New_Data_Bits (
  input  State_4,
  input  BBr,
  input  BS,
  input  [7:0] Current_Data_1,
  input  [7:0] Current_Data_2,
  input  [7:0] Curremt_Data_3,
  input  [7:0] Current_Data_4,
  input  [1:0] Offset,
  input  [31:0] MemInput,
  output [7:0] Output_Data_1,
  output [7:0] Output_Data_2,
  output [7:0] Output_Data_3,
  output [7:0] Output_Data_4,
  output Overwriting
);

  and and_1 (Overwriting, State_4, BBr);
  Multiplexer #(.width(32), .enable("false")) multiplexer_1 (
    .in0({Current_Data_1, Current_Data_2, Curremt_Data_3, Current_Data_4}), .in1(MemInput),
    .out({Output_Data_1, Output_Data_2, Output_Data_3, Output_Data_4}), .sel(Overwriting));

  // Other names for the same wires on the sheet: Current_Data_3[7:0] = Curremt_Data_3; Block_Being_Replaced = BBr;
  //   Block_Selected = BS; LineFromMemInput[31:0] = MemInput; Overwrite_4 = Overwriting

  // Notes on the sheet:
  //   Note: Confused about this circuit. Will be on when we WANT to read or write? See beow "Write" and "Read"
endmodule

module Clock (
  input  State1,
  input  State2,
  input  State3,
  input  State4,
  input  State5,
  input  State6,
  output State1o,
  output State2o,
  output State3o,
  output State4o,
  output State5o,
  output State6o
);

  wire not_1_out, not_2_out, not_3_out, not_4_out, not_5_out;

  not not_1 (not_1_out, State1);
  not not_2 (not_2_out, State2);
  not not_3 (not_3_out, State3);
  not not_4 (not_4_out, State4);
  not not_5 (not_5_out, State5);
  and and_1 (State1o, not_1_out, not_2_out, not_3_out, not_4_out, not_5_out);

  assign State2o = State1;
  assign State3o = State2;
  assign State4o = State3;
  assign State5o = State4;
  assign State6o = State5;
endmodule

module Read_Write (
  input  CpuRead,
  input  CpuWrite,
  input  BS,
  input  State_5,
  input  [7:0] CpuWriteValue,
  input  [7:0] Current_Data_1,
  input  [7:0] Current_Data_2,
  input  [7:0] Current_Data_3,
  input  [7:0] Current_Data_4,
  input  [1:0] Offset,
  input  State_6,
  output [7:0] Output_Data_1,
  output [7:0] Output_Data_2,
  output [7:0] Output_Data_3,
  output [7:0] Output_Data_4,
  output [7:0] Byte_Read
);

  wire Read, Write;
  wire [7:0] multiplexer_1_out, multiplexer_2_out, multiplexer_5_out, multiplexer_6_out, multiplexer_10_out;

  Multiplexer #(.select(2), .width(8), .enable("false")) multiplexer_1 (
    .in0(Current_Data_1), .in1(Current_Data_1), .in2(Current_Data_1), .in3(CpuWriteValue),
    .out(multiplexer_1_out), .sel(Offset));
  Multiplexer #(.select(2), .width(8), .enable("false")) multiplexer_2 (
    .in0(Current_Data_3), .in1(CpuWriteValue), .in2(Current_Data_3), .in3(Current_Data_3),
    .out(multiplexer_2_out), .sel(Offset));
  and and_1 (Write, State_5, CpuWrite, BS);
  Multiplexer #(.width(8), .enable("false")) multiplexer_3 (
    .in0(Current_Data_1), .in1(multiplexer_1_out), .out(Output_Data_1), .sel(Write));
  Multiplexer #(.width(8), .enable("false")) multiplexer_4 (
    .in0(Current_Data_3), .in1(multiplexer_2_out), .out(Output_Data_3), .sel(Write));
  buf and_2 (Read, State_6);  // AND_Gate
  Multiplexer #(.select(2), .width(8), .enable("false")) multiplexer_5 (
    .in0(Current_Data_2), .in1(Current_Data_2), .in2(CpuWriteValue), .in3(Current_Data_2),
    .out(multiplexer_5_out), .sel(Offset));
  Multiplexer #(.select(2), .width(8), .enable("false")) multiplexer_6 (
    .in0(CpuWriteValue), .in1(Current_Data_4), .in2(Current_Data_4), .in3(Current_Data_4),
    .out(multiplexer_6_out), .sel(Offset));
  Multiplexer #(.width(8), .enable("false")) multiplexer_7 (
    .in0(Current_Data_2), .in1(multiplexer_5_out), .out(Output_Data_2), .sel(Write));
  Multiplexer #(.width(8), .enable("false")) multiplexer_8 (
    .in0(Current_Data_4), .in1(multiplexer_6_out), .out(Output_Data_4), .sel(Write));
  Multiplexer #(.select(2), .width(8), .enable("false")) multiplexer_9 (
    .in0(Current_Data_4), .in1(Current_Data_3), .in2(Current_Data_2), .in3(Current_Data_1), .out(Byte_Read),
    .sel(Offset));
  Multiplexer #(.width(8), .enable("false")) multiplexer_10 (.out(multiplexer_10_out), .sel(Read));  // open: in0, in1

  // Other names for the same wires on the sheet: Block_Selected = BS
endmodule
